// Logisim project computerDueAtMidnight.circ as structural Verilog: 32 circuits, main circuit main
module main (
  input  in_1,
  output [63:0] valM_out,
  output [3:0] destM,
  output [63:0] valE_out,
  output [63:0] valA,
  output [3:0] destE,
  output [63:0] valB,
  output cond_out,
  output [63:0] valE,
  output [63:0] valM,
  output [63:0] valP,
  output [3:0] icode,
  output [3:0] ifun,
  output [63:0] valC,
  output [3:0] rA,
  output [3:0] rB,
  output done,
  output [63:0] newPC
);

  wire clock_1_out, decode_1_continue_out, delay2cycles_1_dlay, execute_1_continue_out, fetch_1_continue,
       or_1_out, wholememorystep_1_continue, writebackall_1_enablee;
  wire [3:0] decode_1_icode_out, execute_1_icode;
  wire [63:0] controlled_buffer_1_out, execute_1_vala, PC_q, pcupdate_1_pc;

  Register #(.width(64)) PC (.D(newPC), .en(done), .clk(clock_1_out), .Q(PC_q));  // open: clr
  Clock clock_1 (.out(clock_1_out));
  delay2Cycles delay2cycles_1 (.sig(done), .clk(clock_1_out), .dlay(delay2cycles_1_dlay));
  or or_1 (or_1_out, delay2cycles_1_dlay, in_1);
  fetch fetch_1 (
    .PC(PC_q), .continue_in(or_1_out), .clock(clock_1_out), .valP(valP), .ifun(ifun), .icode(icode),
    .\continue (fetch_1_continue), .valC(valC), .rA(rA), .rB(rB));
  decode decode_1 (
    .dstM(destM), .dstE(destE), .valM(valM_out), .valE(valE_out), .enableE(writebackall_1_enablee),
    .enableM(writebackall_1_enablee), .\continue (fetch_1_continue), .clock(clock_1_out), .icode(icode),
    .rA(rA), .rB(rB), .valA(valA), .valB(valB), .icode_out(decode_1_icode_out),
    .continue_out(decode_1_continue_out));
  execute execute_1 (
    .clock_in(clock_1_out), .continue_in(decode_1_continue_out), .icode_in(decode_1_icode_out),
    .ifun_in(ifun), .valC_in(valC), .valA_in(valA), .valB_in(valB), .continue_out(execute_1_continue_out),
    .cond_out(cond_out), .icode(execute_1_icode), .valE(valE), .valA(execute_1_vala));  // open: ifun
  wholeMemoryStep wholememorystep_1 (
    .icode(execute_1_icode), .valA(execute_1_vala), .valE(valE), .valP(valP), .clk(clock_1_out),
    .continueIn(execute_1_continue_out), .valM(valM), .\continue (wholememorystep_1_continue));
  assign controlled_buffer_1_out = wholememorystep_1_continue ? valP : 64'bz;  // Controlled_Buffer controlled_buffer_1
  writeBackAll writebackall_1 (
    .rA(rA), .rB(rB), .icode(execute_1_icode), .valE(valE), .valM(valM),
    .continue_in(wholememorystep_1_continue), .clk(clock_1_out), .dstM(destM), .dstE(destE),
    .valM_out(valM_out), .valE_out(valE_out), .enableE(writebackall_1_enablee), .continue_out(done));  // open: enableM
  pcUpdate pcupdate_1 (
    .icode(execute_1_icode), .valP(controlled_buffer_1_out), .valM(valM), .valC(valC), .cnd(cond_out),
    .PC(pcupdate_1_pc));
  assign newPC = done ? pcupdate_1_pc : 64'bz;  // Controlled_Buffer controlled_buffer_2

  // Notes on the sheet:
  //   halt
endmodule

module IntructionMem (
  input  [7:0] PC,
  input  CLK,
  output [7:0] B0,
  output [7:0] B1,
  output [7:0] B2,
  output [7:0] B3,
  output [7:0] B4,
  output [7:0] B5,
  output [7:0] B6,
  output [7:0] B7,
  output [7:0] B8,
  output [7:0] B9
);
endmodule

module PCIncrement (
  input  needVal,
  input  Rig,
  input  [7:0] pc,
  output [15:0] valP
);
endmodule

module Align (
  input  [7:0] B1,
  input  [7:0] B2,
  input  [7:0] B3,
  input  [7:0] B4,
  input  [7:0] B5,
  input  [7:0] B6,
  input  [7:0] B7,
  input  [7:0] B8,
  input  [7:0] B9,
  output [3:0] ra,
  output [3:0] rb,
  output [15:0] valC
);
endmodule

module split (
  input  [7:0] B0,
  output [3:0] left,
  output [3:0] right
);


  assign left = B0[3:0];
  assign right = B0[7:4];
endmodule

module fetch (
  input  [63:0] PC,
  input  continue_in,
  input  clock,
  output [63:0] valP,
  output [3:0] ifun,
  output [3:0] icode,
  output \continue ,
  output [63:0] valC,
  output [3:0] rA,
  output [3:0] rB
);

  wire continue_logic_1_continue, controlled_buffer_2_out, decoder_1_out0, decoder_1_out1, decoder_1_out2,
       decoder_1_out3, decoder_1_out4, decoder_1_out5, decoder_1_out6, decoder_1_out7, decoder_1_out8,
       decoder_1_out9, decoder_2_out0, not_1_out, not_2_out, not_3_out, register_4_q;
  wire [3:0] adder_1_out, register_1_q, split_1_left, split_1_right;
  wire [7:0] controlled_buffer_1_out, rom_1_data;
  wire [11:0] calcoffset_1_newpc;

  Adder #(.width(4)) adder_1 (.a(register_1_q), .b(4'b0001), .out(adder_1_out));  // open: cin, cout
  Register #(.width(4)) register_1 (.D(adder_1_out), .en(not_1_out), .clk(clock), .Q(register_1_q), .clr(continue_in));
  not not_1 (not_1_out, continue_logic_1_continue);
  calcOffset calcoffset_1 (.PC(PC[11:0]), .Offset({{8{1'b0}}, register_1_q}), .newPC(calcoffset_1_newpc));
  ROM #(.addrWidth(12)) rom_1 (.addr(calcoffset_1_newpc), .data(rom_1_data));
  assign controlled_buffer_1_out = decoder_1_out0 ? rom_1_data : 8'bz;  // Controlled_Buffer controlled_buffer_1
  Decoder #(.select(4)) decoder_1 (
    .out0(decoder_1_out0), .out1(decoder_1_out1), .out2(decoder_1_out2), .out3(decoder_1_out3),
    .out4(decoder_1_out4), .out5(decoder_1_out5), .out6(decoder_1_out6), .out7(decoder_1_out7),
    .out8(decoder_1_out8), .out9(decoder_1_out9), .sel(register_1_q));  // open: out10, out11, out12, out13, out14, out15, en
  Register #(.width(4)) register_2 (.D(split_1_left), .en(decoder_1_out0), .clk(clock), .Q(ifun));  // open: clr
  split split_1 (.B0(controlled_buffer_1_out), .left(split_1_left), .right(split_1_right));
  valCCalc valccalc_1 (
    .clock(clock), .D(rom_1_data), .r0(decoder_1_out2), .r1(decoder_1_out3), .r2(decoder_1_out4),
    .r3(decoder_1_out5), .r4(decoder_1_out6), .r5(decoder_1_out7), .r6(decoder_1_out8), .r7(decoder_1_out9),
    .r8(decoder_1_out1), .icode(icode), .valC(valC), .rA(rA), .rB(rB));
  Register #(.width(4)) register_3 (.D(split_1_right), .en(decoder_1_out0), .clk(clock), .Q(icode));  // open: clr
  valPCalc valpcalc_1 (.currP(PC[11:0]), .icode(icode), .newPAddr(valP[11:0]));
  continue_logic continue_logic_1 (.icode(icode), .curr_byte(register_1_q), .\continue (continue_logic_1_continue));
  Decoder #(.select(4)) decoder_2 (
    .out0(decoder_2_out0), .sel(icode));  // open: out1, out2, out3, out4, out5, out6, out7, out8, out9, out10, out11, out12, out13, out14, out15, en
  Register #(.width(1)) register_4 (
    .D(continue_logic_1_continue), .en(continue_logic_1_continue), .clk(clock), .Q(register_4_q),
    .clr(continue_in));
  assign controlled_buffer_2_out = not_2_out ? continue_logic_1_continue : 1'bz;  // Controlled_Buffer controlled_buffer_2
  not not_2 (not_2_out, register_4_q);
  assign controlled_buffer_2_out = register_4_q ? 1'b0 : 1'bz;  // Controlled_Buffer controlled_buffer_3
  not not_3 (not_3_out, decoder_2_out0);
  and and_1 (\continue , not_3_out, controlled_buffer_2_out);

  assign valP[63:12] = {52{1'b0}};

  // Notes on the sheet:
  //   The byte we are reading
  //   contents of rom_1 (hex, n*v repeats v):
  //   30 f4 20 4 6*0 30 f8 8*0 30 f3 2 7*0 40 38 8*0 30 f3 2 7*0 40 38 8 7*0 30 f3 3 7*0 40 38 10 7*0 30
  //   f3 4 7*0 40 38 18 7*0 30 f9 20 7*0 30 f3 2 7*0 40 39 8*0 30 f3 2 7*0 40 39 8 7*0 30 f3 2 7*0 40 39
  //   10 7*0 30 f3 3 7*0 40 39 18 7*0 80 fe 7*0 30 fc 69 8*0 30 f0 8*0 30 fb 1 7*0 80 f0 7*0 90 60 70 61
  //   b6 76 f0 7*0 90 30 f1 40 7*0 50 78 8*0 50 69 8*0 80 d2 7*0 20 a 50 78 8 7*0 50 69 10 7*0 80 d2 7*0
  //   60 a 40 a1 8*0 50 78 8*0 50 69 8 7*0 80 d2 7*0 20 a 50 78 8 7*0 50 69 18 7*0 80 d2 7*0 60 a 40 a1 8
  //   7*0 50 78 10 7*0 50 69 8*0 80 d2 7*0 20 a 50 78 18 7*0 50 69 10 7*0 80 d2 7*0 60 a 40 a1 10 7*0 50
  //   78 10 7*0 50 69 8 7*0 80 d2 7*0 20 a 50 78 18 7*0 50 69 18 7*0 80 d2 7*0 60 a 40 a1 18 7*0 90
endmodule

module calcOffset (
  input  [11:0] PC,
  input  [11:0] Offset,
  output [11:0] newPC
);

  Adder #(.width(12)) adder_1 (.a(PC), .b(Offset), .out(newPC));  // open: cin, cout
endmodule

module continue_logic (
  input  [3:0] icode,
  input  [3:0] curr_byte,
  output \continue 
);

  wire and_1_out, and_2_out, and_3_out, and_4_out, decoder_1_out0, decoder_1_out1, decoder_1_out2,
       decoder_1_out3, decoder_1_out4, decoder_1_out5, decoder_1_out6, decoder_1_out7, decoder_1_out8,
       decoder_1_out9, decoder_1_out10, decoder_1_out11, decoder_2_out1, decoder_2_out2, decoder_2_out9,
       decoder_2_out10, or_1_out, or_2_out, or_3_out, or_4_out;

  Decoder #(.select(4)) decoder_1 (
    .out0(decoder_1_out0), .out1(decoder_1_out1), .out2(decoder_1_out2), .out3(decoder_1_out3),
    .out4(decoder_1_out4), .out5(decoder_1_out5), .out6(decoder_1_out6), .out7(decoder_1_out7),
    .out8(decoder_1_out8), .out9(decoder_1_out9), .out10(decoder_1_out10), .out11(decoder_1_out11),
    .sel(icode));  // open: out12, out13, out14, out15, en
  Decoder #(.select(4)) decoder_2 (
    .out1(decoder_2_out1), .out2(decoder_2_out2), .out9(decoder_2_out9), .out10(decoder_2_out10),
    .sel(curr_byte));  // open: out0, out3, out4, out5, out6, out7, out8, out11, out12, out13, out14, out15, en
  or or_1 (or_1_out, decoder_1_out0, decoder_1_out1, decoder_1_out9);
  or or_2 (or_2_out, decoder_1_out2, decoder_1_out6, decoder_1_out10, decoder_1_out11);
  or or_3 (or_3_out, decoder_1_out7, decoder_1_out8);
  or or_4 (or_4_out, decoder_1_out3, decoder_1_out4, decoder_1_out5);
  and and_1 (and_1_out, or_1_out, decoder_2_out1);
  and and_2 (and_2_out, or_2_out, decoder_2_out2);
  and and_3 (and_3_out, or_3_out, decoder_2_out9);
  and and_4 (and_4_out, or_4_out, decoder_2_out10);
  or or_5 (\continue , and_1_out, and_2_out, and_3_out, and_4_out);
endmodule

module valCCalc (
  input  clock,
  input  [7:0] D,
  input  r0,
  input  r1,
  input  r2,
  input  r3,
  input  r4,
  input  r5,
  input  r6,
  input  r7,
  input  r8,
  input  [3:0] icode,
  output [63:0] valC,
  output [3:0] rA,
  output [3:0] rB
);

  wire decoder_1_out2, decoder_1_out3, decoder_1_out4, decoder_1_out5, decoder_1_out6, decoder_1_out10,
       decoder_1_out11, not_1_out, or_1_out;
  wire [7:0] controlled_buffer_3_out, register_1_q, register_2_q, register_3_q, register_4_q, register_5_q,
       register_6_q, register_7_q, register_8_q, register_9_q;

  Register register_1 (.D(D), .en(r0), .clk(clock), .Q(register_1_q));  // open: clr
  Register register_2 (.D(D), .en(r1), .clk(clock), .Q(register_2_q));  // open: clr
  Register register_3 (.D(D), .en(r2), .clk(clock), .Q(register_3_q));  // open: clr
  Register register_4 (.D(D), .en(r3), .clk(clock), .Q(register_4_q));  // open: clr
  Register register_5 (.D(D), .en(r4), .clk(clock), .Q(register_5_q));  // open: clr
  Register register_6 (.D(D), .en(r5), .clk(clock), .Q(register_6_q));  // open: clr
  Register register_7 (.D(D), .en(r6), .clk(clock), .Q(register_7_q));  // open: clr
  Register register_8 (.D(D), .en(r7), .clk(clock), .Q(register_8_q));  // open: clr
  Register register_9 (.D(D), .en(r8), .clk(clock), .Q(register_9_q));  // open: clr
  Decoder #(.select(4)) decoder_1 (
    .out2(decoder_1_out2), .out3(decoder_1_out3), .out4(decoder_1_out4), .out5(decoder_1_out5),
    .out6(decoder_1_out6), .out10(decoder_1_out10), .out11(decoder_1_out11), .sel(icode));  // open: out0, out1, out7, out8, out9, out12, out13, out14, out15, en
  assign valC = or_1_out ? {register_8_q, register_7_q, register_6_q, register_5_q, register_4_q, register_3_q, register_2_q, register_1_q} : 64'bz;  // Controlled_Buffer controlled_buffer_1
  assign valC = not_1_out ? {register_6_q, register_5_q, register_4_q, register_3_q, register_3_q, register_2_q, register_1_q, register_9_q} : 64'bz;  // Controlled_Buffer controlled_buffer_2
  not not_1 (not_1_out, or_1_out);
  assign controlled_buffer_3_out = or_1_out ? register_9_q : 8'bz;  // Controlled_Buffer controlled_buffer_3
  or or_1 (or_1_out, decoder_1_out2, decoder_1_out3, decoder_1_out4, decoder_1_out5, decoder_1_out6, decoder_1_out10, decoder_1_out11);
  split split_1 (.B0(controlled_buffer_3_out), .left(rB), .right(rA));
endmodule

module valPCalc (
  input  [11:0] currP,
  input  [3:0] icode,
  output [11:0] newPAddr
);

  wire decoder_1_out0, decoder_1_out1, decoder_1_out2, decoder_1_out3, decoder_1_out4, decoder_1_out5,
       decoder_1_out6, decoder_1_out7, decoder_1_out8, decoder_1_out9, decoder_1_out10, decoder_1_out11,
       or_1_out, or_2_out, or_3_out, or_4_out;
  wire [11:0] controlled_buffer_1_out;

  Decoder #(.select(4)) decoder_1 (
    .out0(decoder_1_out0), .out1(decoder_1_out1), .out2(decoder_1_out2), .out3(decoder_1_out3),
    .out4(decoder_1_out4), .out5(decoder_1_out5), .out6(decoder_1_out6), .out7(decoder_1_out7),
    .out8(decoder_1_out8), .out9(decoder_1_out9), .out10(decoder_1_out10), .out11(decoder_1_out11),
    .sel(icode));  // open: out12, out13, out14, out15, en
  assign controlled_buffer_1_out = or_1_out ? 12'h1 : 12'bz;  // Controlled_Buffer controlled_buffer_1
  or or_1 (or_1_out, decoder_1_out0, decoder_1_out1, decoder_1_out9);
  or or_2 (or_2_out, decoder_1_out2, decoder_1_out6, decoder_1_out10, decoder_1_out11);
  assign controlled_buffer_1_out = or_2_out ? 12'h2 : 12'bz;  // Controlled_Buffer controlled_buffer_2
  assign controlled_buffer_1_out = or_3_out ? 12'ha : 12'bz;  // Controlled_Buffer controlled_buffer_3
  or or_3 (or_3_out, decoder_1_out3, decoder_1_out4, decoder_1_out5);
  assign controlled_buffer_1_out = or_4_out ? 12'h9 : 12'bz;  // Controlled_Buffer controlled_buffer_4
  or or_4 (or_4_out, decoder_1_out7, decoder_1_out8);
  Adder #(.width(12)) adder_1 (.a(currP), .b(controlled_buffer_1_out), .out(newPAddr));  // open: cin, cout
endmodule

module decode (
  input  [3:0] dstM,
  input  [3:0] dstE,
  input  [63:0] valM,
  input  [63:0] valE,
  input  enableE,
  input  enableM,
  input  \continue ,
  input  clock,
  input  [3:0] icode,
  input  [3:0] rA,
  input  [3:0] rB,
  output [63:0] valA,
  output [63:0] valB,
  output [3:0] icode_out,
  output continue_out
);

  wire controlled_buffer_3_out, not_1_out, register_1_q;
  wire [3:0] address1_logic_1_address1, address2_logic_1_address2, controlled_buffer_1_out,
       controlled_buffer_2_out;
  wire [63:0] reg_file_1_vala, reg_file_1_valb;

  address1_logic address1_logic_1 (.rA(rA), .icode(icode), .address1(address1_logic_1_address1));
  address2_logic address2_logic_1 (.rB(rB), .icode(icode), .address2(address2_logic_1_address2));
  assign controlled_buffer_1_out = \continue  ? address1_logic_1_address1 : 4'bz;  // Controlled_Buffer controlled_buffer_1
  assign controlled_buffer_2_out = \continue  ? address2_logic_1_address2 : 4'bz;  // Controlled_Buffer controlled_buffer_2
  reg_file reg_file_1 (
    .rA(controlled_buffer_1_out), .rB(controlled_buffer_2_out), .dstM(dstM), .dstE(dstE), .valM(valM),
    .valE(valE), .enableA(\continue ), .enableE(enableE), .enableM(enableM), .enableB(\continue ),
    .clk(clock), .valA(reg_file_1_vala), .valB(reg_file_1_valb));
  Register #(.width(1)) register_1 (.D(\continue ), .en(\continue ), .clk(clock), .Q(register_1_q), .clr(\continue ));
  assign controlled_buffer_3_out = register_1_q ? 1'b0 : 1'bz;  // Controlled_Buffer controlled_buffer_3
  assign controlled_buffer_3_out = not_1_out ? \continue  : 1'bz;  // Controlled_Buffer controlled_buffer_4
  not not_1 (not_1_out, register_1_q);
  Register #(.width(64)) register_2 (
    .D(reg_file_1_vala), .en(controlled_buffer_3_out), .clk(clock), .Q(valA));  // open: clr
  Register #(.width(64)) register_3 (
    .D(reg_file_1_valb), .en(controlled_buffer_3_out), .clk(clock), .Q(valB));  // open: clr
  delay2Cycles delay2cycles_1 (.sig(controlled_buffer_3_out), .clk(clock), .dlay(continue_out));

  assign icode_out = icode;
endmodule

module reg_file (
  input  [3:0] rA,
  input  [3:0] rB,
  input  [3:0] dstM,
  input  [3:0] dstE,
  input  [63:0] valM,
  input  [63:0] valE,
  input  enableA,
  input  enableE,
  input  enableM,
  input  enableB,
  input  clk,
  output [63:0] valA,
  output [63:0] valB
);

  wire decoder_1_out0, decoder_1_out1, decoder_1_out2, decoder_1_out3, decoder_1_out4, decoder_1_out5,
       decoder_1_out6, decoder_1_out7, decoder_1_out8, decoder_1_out9, decoder_1_out10, decoder_1_out11,
       decoder_1_out12, decoder_1_out13, decoder_1_out14, decoder_1_out15, decoder_2_out0, decoder_2_out1,
       decoder_2_out2, decoder_2_out3, decoder_2_out4, decoder_2_out5, decoder_2_out6, decoder_2_out7,
       decoder_2_out8, decoder_2_out9, decoder_2_out10, decoder_2_out11, decoder_2_out12, decoder_2_out13,
       decoder_2_out14, decoder_2_out15, decoder_3_out0, decoder_3_out1, decoder_3_out2, decoder_3_out3,
       decoder_3_out4, decoder_3_out5, decoder_3_out6, decoder_3_out7, decoder_3_out8, decoder_3_out9,
       decoder_3_out10, decoder_3_out11, decoder_3_out12, decoder_3_out13, decoder_3_out14, decoder_3_out15,
       decoder_4_out0, decoder_4_out1, decoder_4_out2, decoder_4_out3, decoder_4_out4, decoder_4_out5,
       decoder_4_out6, decoder_4_out7, decoder_4_out8, decoder_4_out9, decoder_4_out10, decoder_4_out11,
       decoder_4_out12, decoder_4_out13, decoder_4_out14, decoder_4_out15, or_1_out, or_2_out, or_3_out,
       or_4_out, or_5_out, or_6_out, or_7_out, or_8_out, or_9_out, or_10_out, or_11_out, or_12_out,
       or_13_out, or_14_out, or_15_out, or_16_out;
  wire [63:0] controlled_buffer_1_out, controlled_buffer_3_out, controlled_buffer_5_out,
       controlled_buffer_7_out, controlled_buffer_9_out, controlled_buffer_11_out, controlled_buffer_13_out,
       controlled_buffer_15_out, controlled_buffer_17_out, controlled_buffer_19_out,
       controlled_buffer_21_out, controlled_buffer_23_out, controlled_buffer_25_out,
       controlled_buffer_27_out, controlled_buffer_29_out, controlled_buffer_31_out, r8_q, r9_q, r10_q,
       r11_q, r12_q, r13_q, r14_q, rax_q, rbp_q, rbx_q, rcx_q, rdi_q, rdx_q, register_1_q, rsi_q, rsp_q;

  Decoder #(.select(4)) decoder_1 (
    .out0(decoder_1_out0), .out1(decoder_1_out1), .out2(decoder_1_out2), .out3(decoder_1_out3),
    .out4(decoder_1_out4), .out5(decoder_1_out5), .out6(decoder_1_out6), .out7(decoder_1_out7),
    .out8(decoder_1_out8), .out9(decoder_1_out9), .out10(decoder_1_out10), .out11(decoder_1_out11),
    .out12(decoder_1_out12), .out13(decoder_1_out13), .out14(decoder_1_out14), .out15(decoder_1_out15),
    .sel(dstE), .en(enableE));
  Decoder #(.select(4)) decoder_2 (
    .out0(decoder_2_out0), .out1(decoder_2_out1), .out2(decoder_2_out2), .out3(decoder_2_out3),
    .out4(decoder_2_out4), .out5(decoder_2_out5), .out6(decoder_2_out6), .out7(decoder_2_out7),
    .out8(decoder_2_out8), .out9(decoder_2_out9), .out10(decoder_2_out10), .out11(decoder_2_out11),
    .out12(decoder_2_out12), .out13(decoder_2_out13), .out14(decoder_2_out14), .out15(decoder_2_out15),
    .sel(dstM), .en(enableM));
  or or_1 (or_1_out, decoder_1_out0, decoder_2_out0);
  or or_2 (or_2_out, decoder_1_out1, decoder_2_out1);
  or or_3 (or_3_out, decoder_1_out2, decoder_2_out2);
  or or_4 (or_4_out, decoder_1_out3, decoder_2_out3);
  or or_5 (or_5_out, decoder_1_out4, decoder_2_out4);
  or or_6 (or_6_out, decoder_1_out5, decoder_2_out5);
  or or_7 (or_7_out, decoder_1_out6, decoder_2_out6);
  or or_8 (or_8_out, decoder_1_out7, decoder_2_out7);
  or or_9 (or_9_out, decoder_1_out8, decoder_2_out8);
  or or_10 (or_10_out, decoder_1_out9, decoder_2_out9);
  or or_11 (or_11_out, decoder_1_out10, decoder_2_out10);
  or or_12 (or_12_out, decoder_1_out11, decoder_2_out11);
  or or_13 (or_13_out, decoder_1_out12, decoder_2_out12);
  or or_14 (or_14_out, decoder_1_out13, decoder_2_out13);
  or or_15 (or_15_out, decoder_1_out14, decoder_2_out14);
  or or_16 (or_16_out, decoder_1_out15, decoder_2_out15);
  Decoder #(.select(4)) decoder_3 (
    .out0(decoder_3_out0), .out1(decoder_3_out1), .out2(decoder_3_out2), .out3(decoder_3_out3),
    .out4(decoder_3_out4), .out5(decoder_3_out5), .out6(decoder_3_out6), .out7(decoder_3_out7),
    .out8(decoder_3_out8), .out9(decoder_3_out9), .out10(decoder_3_out10), .out11(decoder_3_out11),
    .out12(decoder_3_out12), .out13(decoder_3_out13), .out14(decoder_3_out14), .out15(decoder_3_out15),
    .sel(rB), .en(enableB));
  assign controlled_buffer_1_out = decoder_1_out0 ? valE : 64'bz;  // Controlled_Buffer controlled_buffer_1
  assign controlled_buffer_1_out = decoder_2_out0 ? valM : 64'bz;  // Controlled_Buffer controlled_buffer_2
  assign controlled_buffer_3_out = decoder_1_out1 ? valE : 64'bz;  // Controlled_Buffer controlled_buffer_3
  assign controlled_buffer_3_out = decoder_2_out1 ? valM : 64'bz;  // Controlled_Buffer controlled_buffer_4
  assign controlled_buffer_5_out = decoder_1_out2 ? valE : 64'bz;  // Controlled_Buffer controlled_buffer_5
  assign controlled_buffer_5_out = decoder_2_out2 ? valM : 64'bz;  // Controlled_Buffer controlled_buffer_6
  assign controlled_buffer_7_out = decoder_1_out3 ? valE : 64'bz;  // Controlled_Buffer controlled_buffer_7
  assign controlled_buffer_7_out = decoder_2_out3 ? valM : 64'bz;  // Controlled_Buffer controlled_buffer_8
  assign controlled_buffer_9_out = decoder_1_out4 ? valE : 64'bz;  // Controlled_Buffer controlled_buffer_9
  assign controlled_buffer_9_out = decoder_2_out4 ? valM : 64'bz;  // Controlled_Buffer controlled_buffer_10
  assign controlled_buffer_11_out = decoder_1_out5 ? valE : 64'bz;  // Controlled_Buffer controlled_buffer_11
  assign controlled_buffer_11_out = decoder_2_out5 ? valM : 64'bz;  // Controlled_Buffer controlled_buffer_12
  assign controlled_buffer_13_out = decoder_1_out6 ? valE : 64'bz;  // Controlled_Buffer controlled_buffer_13
  assign controlled_buffer_13_out = decoder_2_out6 ? valM : 64'bz;  // Controlled_Buffer controlled_buffer_14
  assign controlled_buffer_15_out = decoder_1_out7 ? valE : 64'bz;  // Controlled_Buffer controlled_buffer_15
  assign controlled_buffer_15_out = decoder_2_out7 ? valM : 64'bz;  // Controlled_Buffer controlled_buffer_16
  assign controlled_buffer_17_out = decoder_1_out8 ? valE : 64'bz;  // Controlled_Buffer controlled_buffer_17
  assign controlled_buffer_17_out = decoder_2_out8 ? valM : 64'bz;  // Controlled_Buffer controlled_buffer_18
  assign controlled_buffer_19_out = decoder_1_out9 ? valE : 64'bz;  // Controlled_Buffer controlled_buffer_19
  assign controlled_buffer_19_out = decoder_2_out9 ? valM : 64'bz;  // Controlled_Buffer controlled_buffer_20
  assign controlled_buffer_21_out = decoder_1_out10 ? valE : 64'bz;  // Controlled_Buffer controlled_buffer_21
  assign controlled_buffer_21_out = decoder_2_out10 ? valM : 64'bz;  // Controlled_Buffer controlled_buffer_22
  assign controlled_buffer_23_out = decoder_1_out11 ? valE : 64'bz;  // Controlled_Buffer controlled_buffer_23
  assign controlled_buffer_23_out = decoder_2_out11 ? valM : 64'bz;  // Controlled_Buffer controlled_buffer_24
  assign controlled_buffer_25_out = decoder_1_out12 ? valE : 64'bz;  // Controlled_Buffer controlled_buffer_25
  assign controlled_buffer_25_out = decoder_2_out12 ? valM : 64'bz;  // Controlled_Buffer controlled_buffer_26
  assign controlled_buffer_27_out = decoder_1_out13 ? valE : 64'bz;  // Controlled_Buffer controlled_buffer_27
  assign controlled_buffer_27_out = decoder_2_out13 ? valM : 64'bz;  // Controlled_Buffer controlled_buffer_28
  assign controlled_buffer_29_out = decoder_1_out14 ? valE : 64'bz;  // Controlled_Buffer controlled_buffer_29
  assign controlled_buffer_29_out = decoder_2_out14 ? valM : 64'bz;  // Controlled_Buffer controlled_buffer_30
  assign controlled_buffer_31_out = decoder_1_out15 ? valE : 64'bz;  // Controlled_Buffer controlled_buffer_31
  assign controlled_buffer_31_out = decoder_2_out15 ? valM : 64'bz;  // Controlled_Buffer controlled_buffer_32
  Register #(.width(64)) rax (.D(controlled_buffer_1_out), .en(or_1_out), .clk(clk), .Q(rax_q));  // open: clr
  Register #(.width(64)) rcx (.D(controlled_buffer_3_out), .en(or_2_out), .clk(clk), .Q(rcx_q));  // open: clr
  Register #(.width(64)) rdx (.D(controlled_buffer_5_out), .en(or_3_out), .clk(clk), .Q(rdx_q));  // open: clr
  Register #(.width(64)) rbx (.D(controlled_buffer_7_out), .en(or_4_out), .clk(clk), .Q(rbx_q));  // open: clr
  Register #(.width(64)) rsp (.D(controlled_buffer_9_out), .en(or_5_out), .clk(clk), .Q(rsp_q));  // open: clr
  Register #(.width(64)) rbp (.D(controlled_buffer_11_out), .en(or_6_out), .clk(clk), .Q(rbp_q));  // open: clr
  Register #(.width(64)) rsi (.D(controlled_buffer_13_out), .en(or_7_out), .clk(clk), .Q(rsi_q));  // open: clr
  Register #(.width(64)) rdi (.D(controlled_buffer_15_out), .en(or_8_out), .clk(clk), .Q(rdi_q));  // open: clr
  Register #(.width(64)) r8 (.D(controlled_buffer_17_out), .en(or_9_out), .clk(clk), .Q(r8_q));  // open: clr
  Register #(.width(64)) r9 (.D(controlled_buffer_19_out), .en(or_10_out), .clk(clk), .Q(r9_q));  // open: clr
  Register #(.width(64)) r10 (.D(controlled_buffer_21_out), .en(or_11_out), .clk(clk), .Q(r10_q));  // open: clr
  Register #(.width(64)) r11 (.D(controlled_buffer_23_out), .en(or_12_out), .clk(clk), .Q(r11_q));  // open: clr
  Register #(.width(64)) r12 (.D(controlled_buffer_25_out), .en(or_13_out), .clk(clk), .Q(r12_q));  // open: clr
  Register #(.width(64)) r13 (.D(controlled_buffer_27_out), .en(or_14_out), .clk(clk), .Q(r13_q));  // open: clr
  Register #(.width(64)) r14 (.D(controlled_buffer_29_out), .en(or_15_out), .clk(clk), .Q(r14_q));  // open: clr
  Register #(.width(64)) register_1 (
    .D(controlled_buffer_31_out), .en(or_16_out), .clk(clk), .Q(register_1_q));  // open: clr
  Decoder #(.select(4)) decoder_4 (
    .out0(decoder_4_out0), .out1(decoder_4_out1), .out2(decoder_4_out2), .out3(decoder_4_out3),
    .out4(decoder_4_out4), .out5(decoder_4_out5), .out6(decoder_4_out6), .out7(decoder_4_out7),
    .out8(decoder_4_out8), .out9(decoder_4_out9), .out10(decoder_4_out10), .out11(decoder_4_out11),
    .out12(decoder_4_out12), .out13(decoder_4_out13), .out14(decoder_4_out14), .out15(decoder_4_out15),
    .sel(rA), .en(enableA));
  assign valA = decoder_4_out15 ? register_1_q : 64'bz;  // Controlled_Buffer controlled_buffer_33
  assign valB = decoder_3_out15 ? register_1_q : 64'bz;  // Controlled_Buffer controlled_buffer_34
  assign valA = decoder_4_out13 ? r13_q : 64'bz;  // Controlled_Buffer controlled_buffer_35
  assign valA = decoder_4_out14 ? r14_q : 64'bz;  // Controlled_Buffer controlled_buffer_36
  assign valB = decoder_3_out14 ? r14_q : 64'bz;  // Controlled_Buffer controlled_buffer_37
  assign valA = decoder_4_out11 ? r11_q : 64'bz;  // Controlled_Buffer controlled_buffer_38
  assign valA = decoder_4_out12 ? r12_q : 64'bz;  // Controlled_Buffer controlled_buffer_39
  assign valB = decoder_3_out12 ? r12_q : 64'bz;  // Controlled_Buffer controlled_buffer_40
  assign valB = decoder_3_out13 ? r13_q : 64'bz;  // Controlled_Buffer controlled_buffer_41
  assign valA = decoder_4_out10 ? r10_q : 64'bz;  // Controlled_Buffer controlled_buffer_42
  assign valB = decoder_3_out10 ? r10_q : 64'bz;  // Controlled_Buffer controlled_buffer_43
  assign valB = decoder_3_out11 ? r11_q : 64'bz;  // Controlled_Buffer controlled_buffer_44
  assign valA = decoder_4_out8 ? r8_q : 64'bz;  // Controlled_Buffer controlled_buffer_45
  assign valA = decoder_4_out9 ? r9_q : 64'bz;  // Controlled_Buffer controlled_buffer_46
  assign valB = decoder_3_out9 ? r9_q : 64'bz;  // Controlled_Buffer controlled_buffer_47
  assign valA = decoder_4_out7 ? rdi_q : 64'bz;  // Controlled_Buffer controlled_buffer_48
  assign valB = decoder_3_out7 ? rdi_q : 64'bz;  // Controlled_Buffer controlled_buffer_49
  assign valB = decoder_3_out8 ? r8_q : 64'bz;  // Controlled_Buffer controlled_buffer_50
  assign valA = decoder_4_out5 ? rbp_q : 64'bz;  // Controlled_Buffer controlled_buffer_51
  assign valA = decoder_4_out6 ? rsi_q : 64'bz;  // Controlled_Buffer controlled_buffer_52
  assign valB = decoder_3_out6 ? rsi_q : 64'bz;  // Controlled_Buffer controlled_buffer_53
  assign valA = decoder_4_out3 ? rbx_q : 64'bz;  // Controlled_Buffer controlled_buffer_54
  assign valA = decoder_4_out4 ? rsp_q : 64'bz;  // Controlled_Buffer controlled_buffer_55
  assign valB = decoder_3_out4 ? rsp_q : 64'bz;  // Controlled_Buffer controlled_buffer_56
  assign valB = decoder_3_out5 ? rbp_q : 64'bz;  // Controlled_Buffer controlled_buffer_57
  assign valA = decoder_4_out2 ? rdx_q : 64'bz;  // Controlled_Buffer controlled_buffer_58
  assign valB = decoder_3_out2 ? rdx_q : 64'bz;  // Controlled_Buffer controlled_buffer_59
  assign valB = decoder_3_out3 ? rbx_q : 64'bz;  // Controlled_Buffer controlled_buffer_60
  assign valA = decoder_4_out0 ? rax_q : 64'bz;  // Controlled_Buffer controlled_buffer_61
  assign valA = decoder_4_out1 ? rcx_q : 64'bz;  // Controlled_Buffer controlled_buffer_62
  assign valB = decoder_3_out1 ? rcx_q : 64'bz;  // Controlled_Buffer controlled_buffer_63
  assign valB = decoder_3_out0 ? rax_q : 64'bz;  // Controlled_Buffer controlled_buffer_64
endmodule

module address1_logic (
  input  [3:0] rA,
  input  [3:0] icode,
  output [3:0] address1
);

  wire decoder_1_out2, decoder_1_out4, decoder_1_out6, decoder_1_out9, decoder_1_out10, decoder_1_out11,
       nor_1_out, or_1_out, or_2_out;

  Decoder #(.select(4)) decoder_1 (
    .out2(decoder_1_out2), .out4(decoder_1_out4), .out6(decoder_1_out6), .out9(decoder_1_out9),
    .out10(decoder_1_out10), .out11(decoder_1_out11), .sel(icode));  // open: out0, out1, out3, out5, out7, out8, out12, out13, out14, out15, en
  or or_1 (or_1_out, decoder_1_out2, decoder_1_out4, decoder_1_out6, decoder_1_out10);
  or or_2 (or_2_out, decoder_1_out9, decoder_1_out11);
  nor nor_1 (nor_1_out, or_1_out, or_2_out);
  assign address1 = nor_1_out ? 4'b1111 : 4'bz;  // Controlled_Buffer controlled_buffer_1
  assign address1 = or_1_out ? rA : 4'bz;  // Controlled_Buffer controlled_buffer_2
  assign address1 = or_2_out ? 4'b0100 : 4'bz;  // Controlled_Buffer controlled_buffer_3
endmodule

module address2_logic (
  input  [3:0] rB,
  input  [3:0] icode,
  output [3:0] address2
);

  wire decoder_1_out4, decoder_1_out5, decoder_1_out6, decoder_1_out8, decoder_1_out9, decoder_1_out10,
       decoder_1_out11, nor_1_out, or_1_out, or_2_out;

  Decoder #(.select(4)) decoder_1 (
    .out4(decoder_1_out4), .out5(decoder_1_out5), .out6(decoder_1_out6), .out8(decoder_1_out8),
    .out9(decoder_1_out9), .out10(decoder_1_out10), .out11(decoder_1_out11), .sel(icode));  // open: out0, out1, out2, out3, out7, out12, out13, out14, out15, en
  or or_1 (or_1_out, decoder_1_out4, decoder_1_out5, decoder_1_out6);
  or or_2 (or_2_out, decoder_1_out8, decoder_1_out9, decoder_1_out10, decoder_1_out11);
  nor nor_1 (nor_1_out, or_1_out, or_2_out);
  assign address2 = nor_1_out ? 4'b1111 : 4'bz;  // Controlled_Buffer controlled_buffer_1
  assign address2 = or_1_out ? rB : 4'bz;  // Controlled_Buffer controlled_buffer_2
  assign address2 = or_2_out ? 4'b0100 : 4'bz;  // Controlled_Buffer controlled_buffer_3
endmodule

module alu (
  input  [63:0] A,
  input  [63:0] B,
  input  [2:0] cmd,
  output [63:0] val_out
);

  wire adder_1_cout, multiplexer_3_out;
  wire [63:0] and_1_out, multiplexer_1_out, multiplexer_2_out, not_1_out, xor_1_out;

  assign and_1_out = A & B;  // AND_Gate and_1, 64 bits wide
  assign xor_1_out = A ^ B;  // XOR_Gate xor_1, 64 bits wide
  assign not_1_out = ~B;  // NOT_Gate not_1, 64 bits wide
  Multiplexer #(.select(3), .width(64)) multiplexer_1 (
    .in1(A), .in2(A), .in3(and_1_out), .in4(xor_1_out), .out(multiplexer_1_out), .sel(cmd));  // open: in0, in5, in6, in7
  Multiplexer #(.select(3), .width(64)) multiplexer_2 (
    .in1(B), .in2(not_1_out), .in3({64{1'b0}}), .in4({64{1'b0}}), .out(multiplexer_2_out), .sel(cmd));  // open: in0, in5, in6, in7
  Multiplexer #(.select(3)) multiplexer_3 (
    .in2(1'b1), .out(multiplexer_3_out), .sel(cmd));  // open: in0, in1, in3, in4, in5, in6, in7
  Adder #(.width(64)) adder_1 (
    .a(multiplexer_1_out), .b(multiplexer_2_out), .out(val_out), .cin(multiplexer_3_out), .cout(adder_1_cout));

  // Notes on the sheet:
  //   0: nothing
  //   1: add (A + B)
  //   2: subtract (A + -B)
  //   3: and (A & B + 0)
  //   4: xor (A xor B + 0)
  //   carry in
endmodule

module execute (
  input  clock_in,
  input  continue_in,
  input  [3:0] icode_in,
  input  [3:0] ifun_in,
  input  [63:0] valC_in,
  input  [63:0] valA_in,
  input  [63:0] valB_in,
  output continue_out,
  output cond_out,
  output [3:0] icode,
  output [3:0] ifun,
  output [63:0] valE,
  output [63:0] valA
);

  wire CF_q, not_1_out, OF_bit_q, set_cc_1_cf, set_cc_1_of_flag, set_cc_1_sf, set_cc_1_write_enable,
       set_cc_1_zf, SF_q, ZF_q;
  wire [2:0] alu_funct_1_alu_op;
  wire [63:0] alu_1_val_out, alu_a_1_alu_a_out, alu_b_1_alu_b_out;

  // NOT_Gate not_1 has open pins: in=open, out=not_1_out
  Controlled_Buffer #(.width(4)) controlled_buffer_1 (.in(4'b1111), .en(not_1_out));  // open: out
  set_cc set_cc_1 (
    .icode(icode_in), .ifun(ifun_in), .a(alu_a_1_alu_a_out), .b(alu_b_1_alu_b_out), .t(alu_1_val_out),
    .write_enable(set_cc_1_write_enable), .CF(set_cc_1_cf), .ZF(set_cc_1_zf), .SF(set_cc_1_sf),
    .OF_flag(set_cc_1_of_flag));
  alu_a alu_a_1 (.valA(valA_in), .valC(valC_in), .icode(icode_in), .alu_a_out(alu_a_1_alu_a_out));
  alu_b alu_b_1 (.valB(valB_in), .icode(icode_in), .alu_b_out(alu_b_1_alu_b_out));
  alu_funct alu_funct_1 (.icode(icode_in), .ifun(ifun_in), .alu_op(alu_funct_1_alu_op));
  Register #(.width(1)) CF (.D(set_cc_1_cf), .en(set_cc_1_write_enable), .clk(clock_in), .Q(CF_q));  // open: clr
  Register #(.width(1)) ZF (.D(set_cc_1_zf), .en(set_cc_1_write_enable), .clk(clock_in), .Q(ZF_q), .clr(1'b0));
  Register #(.width(1)) SF (.D(set_cc_1_sf), .en(set_cc_1_write_enable), .clk(clock_in), .Q(SF_q));  // open: clr
  Register #(.width(1)) OF_bit (
    .D(set_cc_1_of_flag), .en(set_cc_1_write_enable), .clk(clock_in), .Q(OF_bit_q));  // open: clr
  alu alu_1 (.A(alu_b_1_alu_b_out), .B(alu_a_1_alu_a_out), .cmd(alu_funct_1_alu_op), .val_out(alu_1_val_out));
  cond cond_1 (
    .icode_in(icode_in), .ifun_in(ifun_in), .CF(CF_q), .ZF(ZF_q), .SF(SF_q), .OF_flag(OF_bit_q),
    .cond(cond_out));
  Register #(.width(64)) register_1 (.D(alu_1_val_out), .en(continue_in), .clk(continue_in), .Q(valE));  // open: clr
  delay2Cycles delay2cycles_1 (.sig(continue_in), .clk(clock_in), .dlay(continue_out));

  assign icode = icode_in;
  assign ifun = ifun_in;
  assign valA = valA_in;
endmodule

module alu_funct (
  input  [3:0] icode,
  input  [3:0] ifun,
  output [2:0] alu_op
);

  wire and_1_out, and_2_out, and_3_out, and_4_out, decoder_1_out2, decoder_1_out3, decoder_1_out4,
       decoder_1_out5, decoder_1_out6, decoder_1_out8, decoder_1_out9, decoder_1_out10, decoder_1_out11,
       decoder_2_out0, decoder_2_out1, decoder_2_out2, decoder_2_out3, nor_1_out, or_1_out, or_2_out;

  Decoder #(.select(4)) decoder_1 (
    .out2(decoder_1_out2), .out3(decoder_1_out3), .out4(decoder_1_out4), .out5(decoder_1_out5),
    .out6(decoder_1_out6), .out8(decoder_1_out8), .out9(decoder_1_out9), .out10(decoder_1_out10),
    .out11(decoder_1_out11), .sel(icode));  // open: out0, out1, out7, out12, out13, out14, out15, en
  Decoder #(.select(4)) decoder_2 (
    .out0(decoder_2_out0), .out1(decoder_2_out1), .out2(decoder_2_out2), .out3(decoder_2_out3), .sel(ifun));  // open: out4, out5, out6, out7, out8, out9, out10, out11, out12, out13, out14, out15, en
  and and_1 (and_1_out, decoder_1_out6, decoder_2_out0);
  and and_2 (and_2_out, decoder_1_out6, decoder_2_out1);
  or or_1 (or_1_out, decoder_1_out8, and_2_out, decoder_1_out10);
  and and_3 (and_3_out, decoder_1_out6, decoder_2_out2);
  and and_4 (and_4_out, decoder_1_out6, decoder_2_out3);
  or or_2 (or_2_out, decoder_1_out3, decoder_1_out4, decoder_1_out5, decoder_1_out2, decoder_1_out9, decoder_1_out11, and_1_out);
  nor nor_1 (nor_1_out, or_2_out, or_1_out, and_3_out, and_4_out);
  assign alu_op = nor_1_out ? 3'b000 : 3'bz;  // Controlled_Buffer controlled_buffer_1
  assign alu_op = or_2_out ? 3'b001 : 3'bz;  // Controlled_Buffer controlled_buffer_2
  assign alu_op = or_1_out ? 3'b010 : 3'bz;  // Controlled_Buffer controlled_buffer_3
  assign alu_op = and_3_out ? 3'b011 : 3'bz;  // Controlled_Buffer controlled_buffer_4
  assign alu_op = and_4_out ? 3'b100 : 3'bz;  // Controlled_Buffer controlled_buffer_5
  assign alu_op = 1'b0 ? 3'b101 : 3'bz;  // Controlled_Buffer controlled_buffer_6
endmodule

module alu_a (
  input  [63:0] valA,
  input  [63:0] valC,
  input  [3:0] icode,
  output [63:0] alu_a_out
);

  wire decoder_1_out2, decoder_1_out3, decoder_1_out4, decoder_1_out5, decoder_1_out6, decoder_1_out8,
       decoder_1_out9, decoder_1_out10, decoder_1_out11, nor_1_out, or_1_out, or_2_out, or_3_out;

  Decoder #(.select(4)) decoder_1 (
    .out2(decoder_1_out2), .out3(decoder_1_out3), .out4(decoder_1_out4), .out5(decoder_1_out5),
    .out6(decoder_1_out6), .out8(decoder_1_out8), .out9(decoder_1_out9), .out10(decoder_1_out10),
    .out11(decoder_1_out11), .sel(icode));  // open: out0, out1, out7, out12, out13, out14, out15, en
  or or_1 (or_1_out, decoder_1_out3, decoder_1_out4, decoder_1_out5);
  or or_2 (or_2_out, decoder_1_out6, decoder_1_out2);
  or or_3 (or_3_out, decoder_1_out8, decoder_1_out9, decoder_1_out10, decoder_1_out11);
  nor nor_1 (nor_1_out, or_1_out, or_3_out, or_2_out);
  assign alu_a_out = nor_1_out ? {64{1'b0}} : 64'bz;  // Controlled_Buffer controlled_buffer_1
  assign alu_a_out = or_3_out ? 64'h8 : 64'bz;  // Controlled_Buffer controlled_buffer_2
  assign alu_a_out = or_2_out ? valA : 64'bz;  // Controlled_Buffer controlled_buffer_3
  assign alu_a_out = or_1_out ? valC : 64'bz;  // Controlled_Buffer controlled_buffer_4
endmodule

module alu_b (
  input  [63:0] valB,
  input  [3:0] icode,
  output [63:0] alu_b_out
);

  wire decoder_1_out4, decoder_1_out5, decoder_1_out6, decoder_1_out8, decoder_1_out9, decoder_1_out10,
       decoder_1_out11, not_1_out, or_1_out;

  Decoder #(.select(4)) decoder_1 (
    .out4(decoder_1_out4), .out5(decoder_1_out5), .out6(decoder_1_out6), .out8(decoder_1_out8),
    .out9(decoder_1_out9), .out10(decoder_1_out10), .out11(decoder_1_out11), .sel(icode));  // open: out0, out1, out2, out3, out7, out12, out13, out14, out15, en
  or or_1 (or_1_out, decoder_1_out4, decoder_1_out5, decoder_1_out6, decoder_1_out8, decoder_1_out9, decoder_1_out10, decoder_1_out11);
  not not_1 (not_1_out, or_1_out);
  assign alu_b_out = not_1_out ? {64{1'b0}} : 64'bz;  // Controlled_Buffer controlled_buffer_1
  assign alu_b_out = or_1_out ? valB : 64'bz;  // Controlled_Buffer controlled_buffer_2
endmodule

module cond (
  input  [3:0] icode_in,
  input  [3:0] ifun_in,
  input  CF,
  input  ZF,
  input  SF,
  input  OF_flag,
  output cond
);

  wire and_1_out, and_2_out, and_3_out, and_4_out, and_5_out, and_6_out, and_7_out, and_8_out, and_9_out,
       decoder_1_out2, decoder_1_out7, decoder_2_out0, decoder_2_out1, decoder_2_out2, decoder_2_out3,
       decoder_2_out4, decoder_2_out5, decoder_2_out6, nand_1_out, nand_2_out, not_1_out, not_2_out,
       or_1_out, or_2_out, or_3_out;

  Decoder #(.select(4)) decoder_1 (
    .out2(decoder_1_out2), .out7(decoder_1_out7), .sel(icode_in));  // open: out0, out1, out3, out4, out5, out6, out8, out9, out10, out11, out12, out13, out14, out15, en
  Decoder #(.select(4)) decoder_2 (
    .out0(decoder_2_out0), .out1(decoder_2_out1), .out2(decoder_2_out2), .out3(decoder_2_out3),
    .out4(decoder_2_out4), .out5(decoder_2_out5), .out6(decoder_2_out6), .sel(ifun_in));  // open: out7, out8, out9, out10, out11, out12, out13, out14, out15, en
  or or_1 (or_1_out, decoder_1_out2, decoder_1_out7);
  and and_1 (and_1_out, SF, OF_flag);
  and and_2 (and_2_out, SF, OF_flag);
  nand nand_1 (nand_1_out, SF, OF_flag);
  nand nand_2 (nand_2_out, SF, OF_flag);
  or or_2 (or_2_out, and_1_out, ZF);
  not not_1 (not_1_out, ZF);
  and and_3 (and_3_out, nand_2_out, not_2_out);
  not not_2 (not_2_out, ZF);
  and and_4 (and_4_out, decoder_2_out1, or_2_out);
  and and_5 (and_5_out, decoder_2_out2, and_2_out);
  and and_6 (and_6_out, decoder_2_out3, ZF);
  and and_7 (and_7_out, decoder_2_out4, not_1_out);
  and and_8 (and_8_out, decoder_2_out5, nand_1_out);
  and and_9 (and_9_out, decoder_2_out6, and_3_out);
  or or_3 (or_3_out, decoder_2_out0, and_4_out, and_5_out, and_6_out, and_7_out, and_8_out, and_9_out);
  and and_10 (cond, or_1_out, or_3_out);

  // Notes on the sheet:
  //   jmp
  //   jle
  //   jl
  //   je
  //   jne
  //   jge
  //   jg
endmodule

module set_cc (
  input  [3:0] icode,
  input  [3:0] ifun,
  input  [63:0] a,
  input  [63:0] b,
  input  [63:0] t,
  output write_enable,
  output CF,
  output ZF,
  output SF,
  output OF_flag
);

  wire comparator_1_lt, comparator_2_lt, comparator_3_lt, comparator_4_lt, decoder_2_out6, not_2_out,
       not_3_out, xor_1_out, xor_2_out;
  wire [63:0] adder_1_out, controlled_buffer_1_out, not_1_out;

  Decoder #(.select(4)) decoder_1 (
    .out6(write_enable), .sel(icode));  // open: out0, out1, out2, out3, out4, out5, out7, out8, out9, out10, out11, out12, out13, out14, out15, en
  Decoder #(.select(4)) decoder_2 (
    .out6(decoder_2_out6), .sel(ifun));  // open: out0, out1, out2, out3, out4, out5, out7, out8, out9, out10, out11, out12, out13, out14, out15, en
  assign not_1_out = ~a;  // NOT_Gate not_1, 64 bits wide
  assign controlled_buffer_1_out = decoder_2_out6 ? adder_1_out : 64'bz;  // Controlled_Buffer controlled_buffer_1
  Adder #(.width(64)) adder_1 (.a(64'h1), .b(not_1_out), .out(adder_1_out));  // open: cin, cout
  not not_2 (not_2_out, decoder_2_out6);
  assign controlled_buffer_1_out = not_2_out ? a : 64'bz;  // Controlled_Buffer controlled_buffer_2
  Comparator #(.width(64)) comparator_1 (
    .a(controlled_buffer_1_out), .b({64{1'b0}}), .lt(comparator_1_lt));  // open: gt, eq
  Comparator #(.width(64)) comparator_2 (.a(b), .b({64{1'b0}}), .lt(comparator_2_lt));  // open: gt, eq
  Comparator #(.width(64)) comparator_3 (.a(t), .b({64{1'b0}}), .lt(comparator_3_lt));  // open: gt, eq
  Comparator #(.width(64)) comparator_4 (
    .a(controlled_buffer_1_out), .b({64{1'b0}}), .lt(comparator_4_lt));  // open: gt, eq
  not not_3 (not_3_out, xor_1_out);
  xor xor_1 (xor_1_out, comparator_1_lt, comparator_2_lt);
  xor xor_2 (xor_2_out, comparator_3_lt, comparator_4_lt);
  Comparator #(.width(64)) comparator_5 (.a(t), .b(controlled_buffer_1_out), .lt(CF));  // open: gt, eq
  Comparator #(.width(64)) comparator_6 (.a(t), .b({64{1'b0}}), .eq(ZF));  // open: gt, lt
  Comparator #(.width(64)) comparator_7 (.a(t), .b({64{1'b0}}), .lt(SF));  // open: gt, eq
  and and_1 (OF_flag, not_3_out, xor_2_out);

  // Notes on the sheet:
  //   Set if icode == 6
  //   Negate a for sub
  //   CF: unsigned Carry
  //   ZF: output is 0
  //   SF: output < 0
  //   OF: overflow detected
endmodule

module readWriteIO (
  input  [3:0] icode,
  output write,
  output read
);

  wire and_1_out, and_2_out, and_3_out, and_4_out, not_1_out, not_2_out, not_3_out, not_4_out;

  not not_1 (not_1_out, icode[3]);
  not not_2 (not_2_out, icode[2]);
  not not_3 (not_3_out, icode[1]);
  not not_4 (not_4_out, icode[0]);
  and and_1 (and_1_out, not_1_out, icode[2], not_3_out, not_4_out);
  and and_2 (and_2_out, icode[3], not_2_out, not_4_out);
  and and_3 (and_3_out, not_1_out, icode[2], not_3_out, icode[0]);
  and and_4 (and_4_out, icode[3], not_2_out, icode[0]);
  or or_1 (write, and_1_out, and_2_out);
  or or_2 (read, and_3_out, and_4_out);
endmodule

module dataIO (
  input  [63:0] valA,
  input  [63:0] valP,
  input  [3:0] icode,
  output [63:0] data
);

  wire and_1_out, and_2_out, and_3_out, not_1_out, not_2_out, not_3_out, not_4_out, or_1_out;

  not not_1 (not_1_out, icode[3]);
  not not_2 (not_2_out, icode[2]);
  not not_3 (not_3_out, icode[1]);
  not not_4 (not_4_out, icode[0]);
  and and_1 (and_1_out, not_1_out, icode[2], not_3_out, not_4_out);
  and and_2 (and_2_out, icode[3], not_2_out, icode[1], not_4_out);
  and and_3 (and_3_out, icode[3], not_2_out, not_3_out, not_4_out);
  assign data = or_1_out ? valA : 64'bz;  // Controlled_Buffer controlled_buffer_1
  or or_1 (or_1_out, and_1_out, and_2_out);
  assign data = and_3_out ? valP : 64'bz;  // Controlled_Buffer controlled_buffer_2
endmodule

module masterIO (
  input  [3:0] icode,
  input  [63:0] valA,
  input  [63:0] valE,
  input  [63:0] valP,
  input  continueIn,
  input  clk,
  input  reset,
  output [11:0] address,
  output write,
  output read,
  output [7:0] data,
  output continueOut,
  output [3:0] stepNumber
);

  wire decoder_1_out1, decoder_1_out2, decoder_1_out3, decoder_1_out4, decoder_1_out5, decoder_1_out6,
       decoder_1_out7, decoder_1_out8;
  wire [11:0] controlled_buffer_1_out, memstepaddio_1_address;
  wire [63:0] dataio_1_data;

  readWriteIO readwriteio_1 (.icode(icode), .write(write), .read(read));
  memStepAddIO memstepaddio_1 (.valA(valA), .valE(valE), .icode(icode), .address(memstepaddio_1_address));
  dataIO dataio_1 (.valA(valA), .valP(valP), .icode(icode), .data(dataio_1_data));
  countTo8 countto8_1 (.continueIn(continueIn), .clk(clk), .reset(reset), .out_4(stepNumber));
  Decoder #(.select(4)) decoder_1 (
    .out1(decoder_1_out1), .out2(decoder_1_out2), .out3(decoder_1_out3), .out4(decoder_1_out4),
    .out5(decoder_1_out5), .out6(decoder_1_out6), .out7(decoder_1_out7), .out8(decoder_1_out8),
    .out9(continueOut), .sel(stepNumber), .en(1'b1));  // open: out0, out10, out11, out12, out13, out14, out15
  assign controlled_buffer_1_out = decoder_1_out1 ? {12{1'b0}} : 12'bz;  // Controlled_Buffer controlled_buffer_1
  assign controlled_buffer_1_out = decoder_1_out2 ? 12'h1 : 12'bz;  // Controlled_Buffer controlled_buffer_2
  assign controlled_buffer_1_out = decoder_1_out3 ? 12'h2 : 12'bz;  // Controlled_Buffer controlled_buffer_3
  assign data = decoder_1_out1 ? dataio_1_data[7:0] : 8'bz;  // Controlled_Buffer controlled_buffer_4
  assign data = decoder_1_out2 ? dataio_1_data[15:8] : 8'bz;  // Controlled_Buffer controlled_buffer_5
  assign data = decoder_1_out3 ? dataio_1_data[23:16] : 8'bz;  // Controlled_Buffer controlled_buffer_6
  assign controlled_buffer_1_out = decoder_1_out4 ? 12'h3 : 12'bz;  // Controlled_Buffer controlled_buffer_7
  assign controlled_buffer_1_out = decoder_1_out5 ? 12'h4 : 12'bz;  // Controlled_Buffer controlled_buffer_8
  assign controlled_buffer_1_out = decoder_1_out6 ? 12'h5 : 12'bz;  // Controlled_Buffer controlled_buffer_9
  assign controlled_buffer_1_out = decoder_1_out7 ? 12'h6 : 12'bz;  // Controlled_Buffer controlled_buffer_10
  assign data = decoder_1_out4 ? dataio_1_data[31:24] : 8'bz;  // Controlled_Buffer controlled_buffer_11
  assign data = decoder_1_out5 ? dataio_1_data[39:32] : 8'bz;  // Controlled_Buffer controlled_buffer_12
  assign data = decoder_1_out6 ? dataio_1_data[47:40] : 8'bz;  // Controlled_Buffer controlled_buffer_13
  assign data = decoder_1_out7 ? dataio_1_data[55:48] : 8'bz;  // Controlled_Buffer controlled_buffer_14
  assign controlled_buffer_1_out = decoder_1_out8 ? 12'h7 : 12'bz;  // Controlled_Buffer controlled_buffer_15
  assign controlled_buffer_1_out = continueOut ? 12'h7 : 12'bz;  // Controlled_Buffer controlled_buffer_16
  assign data = decoder_1_out8 ? dataio_1_data[63:56] : 8'bz;  // Controlled_Buffer controlled_buffer_17
  assign data = continueOut ? data : 8'bz;  // Controlled_Buffer controlled_buffer_18
  Adder #(.width(12)) adder_1 (
    .a(controlled_buffer_1_out), .b(memstepaddio_1_address), .out(address));  // open: cin, cout
endmodule

module countTo8 (
  input  continueIn,
  input  clk,
  input  reset,
  output [3:0] out_4
);

  wire comparator_1_eq, comparator_1_gt, not_1_out, not_2_out, not_3_out, not_4_out, not_5_out;
  wire [3:0] adder_1_out, controlled_buffer_1_out, controlled_buffer_2_out, register_1_q;

  not not_1 (not_1_out, clk);
  assign controlled_buffer_1_out = comparator_1_gt ? register_1_q : 4'bz;  // Controlled_Buffer controlled_buffer_1
  assign controlled_buffer_2_out = not_2_out ? {3'b000, continueIn} : 4'bz;  // Controlled_Buffer controlled_buffer_2
  not not_2 (not_2_out, not_1_out);
  assign controlled_buffer_1_out = comparator_1_eq ? 4'b0000 : 4'bz;  // Controlled_Buffer controlled_buffer_3
  Adder #(.width(4)) adder_1 (
    .a(controlled_buffer_1_out), .b(controlled_buffer_2_out), .out(adder_1_out));  // open: cin, cout
  Comparator #(.mode("unsigned"), .width(4)) comparator_1 (
    .a(4'b1001), .b(register_1_q), .gt(comparator_1_gt), .eq(comparator_1_eq));  // open: lt
  Register #(.width(4)) register_1 (.D(adder_1_out), .en(not_3_out), .clk(not_4_out), .Q(register_1_q), .clr(reset));
  not not_3 (not_3_out, clk);
  not not_4 (not_4_out, clk);
  assign out_4 = continueIn ? register_1_q : 4'bz;  // Controlled_Buffer controlled_buffer_4
  not not_5 (not_5_out, continueIn);
  assign out_4 = not_5_out ? 4'b0000 : 4'bz;  // Controlled_Buffer controlled_buffer_5
endmodule

module wholeMemoryStep (
  input  [3:0] icode,
  input  [63:0] valA,
  input  [63:0] valE,
  input  [63:0] valP,
  input  clk,
  input  continueIn,
  output [63:0] valM,
  output \continue 
);

  wire decoder_1_out2, decoder_1_out3, decoder_1_out4, decoder_1_out5, decoder_1_out6, decoder_1_out7,
       decoder_1_out8, decoder_1_out9, masterio_1_continueout, masterio_1_read, masterio_1_write, or_1_out,
       or_2_out, register_1_q;
  wire [3:0] masterio_1_stepnumber;
  wire [7:0] masterio_1_data, ram_1_dout;
  wire [11:0] masterio_1_address;

  or or_1 (or_1_out, continueIn, masterio_1_continueout);
  Register #(.width(1)) register_1 (.D(continueIn), .en(or_1_out), .clk(clk), .Q(register_1_q));  // open: clr
  masterIO masterio_1 (
    .icode(icode), .valA(valA), .valE(valE), .valP(valP), .continueIn(register_1_q), .clk(clk),
    .reset(continueIn), .address(masterio_1_address), .write(masterio_1_write), .read(masterio_1_read),
    .data(masterio_1_data), .continueOut(masterio_1_continueout), .stepNumber(masterio_1_stepnumber));
  RAM #(.addrWidth(12)) ram_1 (
    .addr(masterio_1_address), .we(masterio_1_write), .oe(masterio_1_read), .clk(clk), .din(masterio_1_data),
    .dout(ram_1_dout));
  Decoder #(.select(4)) decoder_1 (
    .out2(decoder_1_out2), .out3(decoder_1_out3), .out4(decoder_1_out4), .out5(decoder_1_out5),
    .out6(decoder_1_out6), .out7(decoder_1_out7), .out8(decoder_1_out8), .out9(decoder_1_out9),
    .sel(masterio_1_stepnumber));  // open: out0, out1, out10, out11, out12, out13, out14, out15, en
  Register register_2 (.D(ram_1_dout), .en(decoder_1_out2), .clk(clk), .Q(valM[7:0]));  // open: clr
  Register register_3 (.D(ram_1_dout), .en(decoder_1_out3), .clk(clk), .Q(valM[15:8]));  // open: clr
  Register register_4 (.D(ram_1_dout), .en(decoder_1_out4), .clk(clk), .Q(valM[23:16]));  // open: clr
  Register register_5 (.D(ram_1_dout), .en(decoder_1_out5), .clk(clk), .Q(valM[31:24]));  // open: clr
  Register register_6 (.D(ram_1_dout), .en(decoder_1_out6), .clk(clk), .Q(valM[39:32]));  // open: clr
  Register register_7 (.D(ram_1_dout), .en(decoder_1_out7), .clk(clk), .Q(valM[47:40]));  // open: clr
  Register register_8 (.D(ram_1_dout), .en(decoder_1_out8), .clk(clk), .Q(valM[55:48]));  // open: clr
  Register register_9 (.D(ram_1_dout), .en(decoder_1_out9), .clk(clk), .Q(valM[63:56]));  // open: clr
  Register #(.width(1)) register_10 (.D(decoder_1_out9), .en(or_2_out), .clk(clk), .Q(\continue ));  // open: clr
  or or_2 (or_2_out, decoder_1_out9, \continue );
endmodule

module memStepAddIO (
  input  [63:0] valA,
  input  [63:0] valE,
  input  [3:0] icode,
  output [11:0] address
);

  wire and_1_out, and_2_out, and_3_out, not_1_out, not_2_out, not_3_out, not_4_out, or_1_out;
  wire [63:12] controlled_buffer_1_out;

  not not_1 (not_1_out, icode[3]);
  not not_2 (not_2_out, icode[2]);
  not not_3 (not_3_out, icode[1]);
  not not_4 (not_4_out, icode[0]);
  and and_1 (and_1_out, icode[3], not_2_out, icode[0]);
  and and_2 (and_2_out, not_1_out, icode[2], not_3_out);
  and and_3 (and_3_out, icode[3], not_2_out, not_4_out);
  assign {controlled_buffer_1_out, address} = and_1_out ? valA : 64'bz;  // Controlled_Buffer controlled_buffer_1
  or or_1 (or_1_out, and_2_out, and_3_out);
  assign {controlled_buffer_1_out, address} = or_1_out ? valE : 64'bz;  // Controlled_Buffer controlled_buffer_2
endmodule

module addressIO (
  input  [3:0] rA,
  input  [3:0] rB,
  input  [3:0] rsp,
  input  [3:0] icode,
  input  cycleNum,
  output [3:0] address
);

  wire and_1_out, and_2_out, and_3_out, and_4_out, and_5_out, and_6_out, and_7_out, and_8_out, and_9_out,
       not_1_out, not_2_out, not_3_out, not_4_out, not_5_out, not_6_out, or_1_out, or_2_out, or_3_out,
       or_4_out;

  not not_1 (not_1_out, icode[3]);
  not not_2 (not_2_out, icode[2]);
  not not_3 (not_3_out, icode[1]);
  not not_4 (not_4_out, icode[0]);
  not not_5 (not_5_out, icode[2]);
  and and_1 (and_1_out, not_1_out, not_2_out, icode[1]);
  and and_2 (and_2_out, not_1_out, icode[1], not_4_out);
  and and_3 (and_3_out, not_1_out, icode[2], not_3_out, icode[0]);
  and and_4 (and_4_out, icode[3], not_2_out, not_3_out);
  and and_5 (and_5_out, icode[3], not_2_out, not_4_out);
  and and_6 (and_6_out, icode[0], icode[1], icode[3]);
  buf and_7 (and_7_out, not_5_out);  // AND_Gate
  not not_6 (not_6_out, cycleNum);
  assign address = or_2_out ? rA : 4'bz;  // Controlled_Buffer controlled_buffer_1
  or or_1 (or_1_out, and_1_out, and_2_out);
  or or_2 (or_2_out, and_3_out, and_8_out);
  or or_3 (or_3_out, and_4_out, and_5_out);
  and and_8 (and_8_out, and_6_out, cycleNum, and_7_out);
  and and_9 (and_9_out, and_6_out, and_7_out, not_6_out);
  assign address = or_1_out ? rB : 4'bz;  // Controlled_Buffer controlled_buffer_2
  assign address = or_4_out ? rsp : 4'bz;  // Controlled_Buffer controlled_buffer_3
  or or_4 (or_4_out, or_3_out, and_9_out);
endmodule

module valueIO (
  input  [3:0] icode,
  input  [63:0] valE,
  input  [63:0] valM,
  input  cycleNum,
  output [63:0] data
);

  wire and_1_out, and_2_out, and_3_out, and_4_out, and_5_out, and_6_out, and_7_out, and_8_out, and_9_out,
       not_1_out, not_2_out, not_3_out, not_4_out, not_5_out, not_6_out, or_1_out, or_2_out, or_3_out;

  not not_1 (not_1_out, icode[3]);
  not not_2 (not_2_out, icode[2]);
  not not_3 (not_3_out, icode[1]);
  not not_4 (not_4_out, icode[0]);
  not not_5 (not_5_out, icode[2]);
  and and_1 (and_1_out, not_1_out, not_2_out, icode[1]);
  and and_2 (and_2_out, not_1_out, icode[1], not_4_out);
  and and_3 (and_3_out, not_2_out, icode[1], not_4_out);
  and and_4 (and_4_out, icode[3], not_2_out, not_3_out);
  and and_5 (and_5_out, not_1_out, icode[2], not_3_out, icode[0]);
  and and_6 (and_6_out, icode[0], icode[1], icode[3]);
  buf and_7 (and_7_out, not_5_out);  // AND_Gate
  not not_6 (not_6_out, cycleNum);
  or or_1 (or_1_out, or_2_out, and_9_out);
  or or_2 (or_2_out, and_1_out, and_2_out, and_3_out, and_4_out);
  and and_8 (and_8_out, and_6_out, cycleNum, and_7_out);
  and and_9 (and_9_out, and_6_out, and_7_out, not_6_out);
  assign data = or_1_out ? valE : 64'bz;  // Controlled_Buffer controlled_buffer_1
  assign data = or_3_out ? valM : 64'bz;  // Controlled_Buffer controlled_buffer_2
  or or_3 (or_3_out, and_5_out, and_8_out);
endmodule

module writeBackAll (
  input  [3:0] rA,
  input  [3:0] rB,
  input  [3:0] icode,
  input  [63:0] valE,
  input  [63:0] valM,
  input  continue_in,
  input  clk,
  output [3:0] dstM,
  output [3:0] dstE,
  output [63:0] valM_out,
  output [63:0] valE_out,
  output enableE,
  output enableM,
  output continue_out
);

  wire decoder_1_out0, decoder_1_out1, decoder_1_out4, decoder_1_out7, not_1_out, not_2_out, or_1_out,
       register_1_q;

  Decoder #(.select(4)) decoder_1 (
    .out0(decoder_1_out0), .out1(decoder_1_out1), .out4(decoder_1_out4), .out7(decoder_1_out7), .sel(icode));  // open: out2, out3, out5, out6, out8, out9, out10, out11, out12, out13, out14, out15, en
  or or_1 (or_1_out, decoder_1_out0, decoder_1_out1, decoder_1_out4, decoder_1_out7);
  addressIO addressio_1 (.rA(rA), .rB(rB), .rsp(4'b0100), .icode(icode), .cycleNum(1'b0), .address(dstM));
  valueIO valueio_1 (.icode(icode), .valE(valE), .valM(valM), .cycleNum(1'b0), .data(valM_out));
  addressIO addressio_2 (.rA(rA), .rB(rB), .rsp(4'b0100), .icode(icode), .cycleNum(1'b1), .address(dstE));
  valueIO valueio_2 (.icode(icode), .valE(valE), .valM(valM), .cycleNum(1'b1), .data(valE_out));
  not not_1 (not_1_out, or_1_out);
  and and_1 (enableE, continue_in, not_1_out);
  Register #(.width(1)) register_1 (
    .D(continue_in), .en(continue_in), .Q(register_1_q), .clr(continue_in));  // open: clk
  assign continue_out = register_1_q ? 1'b0 : 1'bz;  // Controlled_Buffer controlled_buffer_1
  assign continue_out = not_2_out ? continue_in : 1'bz;  // Controlled_Buffer controlled_buffer_2
  not not_2 (not_2_out, register_1_q);

  assign enableM = enableE;
endmodule

module pcUpdate (
  input  [3:0] icode,
  input  [63:0] valP,
  input  [63:0] valM,
  input  [63:0] valC,
  input  cnd,
  output [63:0] PC
);

  wire and_1_out, and_2_out, decoder_1_out0, decoder_1_out1, decoder_1_out2, decoder_1_out3, decoder_1_out4,
       decoder_1_out5, decoder_1_out6, decoder_1_out7, decoder_1_out8, decoder_1_out9, decoder_1_out10,
       decoder_1_out11, not_1_out, or_1_out, or_2_out, or_3_out;

  Decoder #(.select(4)) decoder_1 (
    .out0(decoder_1_out0), .out1(decoder_1_out1), .out2(decoder_1_out2), .out3(decoder_1_out3),
    .out4(decoder_1_out4), .out5(decoder_1_out5), .out6(decoder_1_out6), .out7(decoder_1_out7),
    .out8(decoder_1_out8), .out9(decoder_1_out9), .out10(decoder_1_out10), .out11(decoder_1_out11),
    .sel(icode));  // open: out12, out13, out14, out15, en
  not not_1 (not_1_out, cnd);
  and and_1 (and_1_out, decoder_1_out7, cnd);
  and and_2 (and_2_out, decoder_1_out7, not_1_out);
  or or_1 (or_1_out, decoder_1_out1, decoder_1_out2, decoder_1_out3, decoder_1_out4, decoder_1_out5, decoder_1_out6, decoder_1_out10, decoder_1_out11);
  assign PC = decoder_1_out0 ? {64{1'b0}} : 64'bz;  // Controlled_Buffer controlled_buffer_1
  or or_2 (or_2_out, or_1_out, and_2_out);
  assign PC = or_2_out ? valP : 64'bz;  // Controlled_Buffer controlled_buffer_2
  assign PC = decoder_1_out9 ? valM : 64'bz;  // Controlled_Buffer controlled_buffer_3
  or or_3 (or_3_out, and_1_out, decoder_1_out8);
  assign PC = or_3_out ? valC : 64'bz;  // Controlled_Buffer controlled_buffer_4
endmodule

module delay2Cycles (
  input  sig,
  input  clk,
  output dlay
);

  wire and_1_out, not_1_out, register_1_q, register_3_q;

  not not_1 (not_1_out, sig);
  Register #(.width(1)) register_1 (.D(sig), .en(sig), .clk(clk), .Q(register_1_q), .clr(and_1_out));
  and and_1 (and_1_out, not_1_out, register_3_q);
  Register #(.width(1)) register_2 (.D(register_1_q), .en(register_1_q), .clk(clk), .Q(dlay), .clr(and_1_out));
  Register #(.width(1)) register_3 (.D(dlay), .en(dlay), .clk(clk), .Q(register_3_q), .clr(sig));
endmodule
